// Logisim project disaster_warning_device.circ as structural Verilog: 8 circuits, main circuit DEVICE
module DEVICE (
  input  MODE,
  input  [1:0] R1R0,
  input  [1:0] S1S0,
  input  [1:0] W1W0,
  input  [1:0] L1L0
);

  wire cyclone_1_cyclone, decoder_1_cyclone, decoder_1_earthquake, decoder_1_flood, decoder_1_tsunami,
       earthquake_1_earthquake, flood_1_flood, mode_1_output, mode_2_output, mode_3_output, mode_4_output,
       not_1_out, not_2_out, priority_encoder_1_safe___danger, tsunami_1_tsunami;
  wire [1:0] priority_encoder_1_y1_y0;

  flood flood_1 (.R1R0(R1R0), .S1S0(S1S0), .W1W0(W1W0), .L1L0(L1L0), .FLOOD(flood_1_flood));
  cyclone cyclone_1 (.R1R0(R1R0), .S1S0(S1S0), .W1W0(W1W0), .L1L0(L1L0), .CYCLONE(cyclone_1_cyclone));
  earthquake earthquake_1 (.R1R0(R1R0), .S1S0(S1S0), .W1W0(W1W0), .L1L0(L1L0), .EARTHQUAKE(earthquake_1_earthquake));
  tsunami tsunami_1 (.R1R0(R1R0), .S1S0(S1S0), .W1W0(W1W0), .L1L0(L1L0), .TSUNAMI(tsunami_1_tsunami));
  not not_1 (not_1_out, MODE);
  priority_encoder priority_encoder_1 (
    .F(flood_1_flood), .C(cyclone_1_cyclone), .E(earthquake_1_earthquake), .T(tsunami_1_tsunami),
    .SAFE___DANGER(priority_encoder_1_safe___danger), .Y1_Y0(priority_encoder_1_y1_y0));
  not not_2 (not_2_out, priority_encoder_1_safe___danger);
  decoder decoder_1 (
    .Safe___Danger(priority_encoder_1_safe___danger), .Y1_Y0(priority_encoder_1_y1_y0),
    .FLOOD(decoder_1_flood), .CYCLONE(decoder_1_cyclone), .EARTHQUAKE(decoder_1_earthquake),
    .TSUNAMI(decoder_1_tsunami));
  LED SAFE (.in(not_2_out));
  LED DANGER (.in(priority_encoder_1_safe___danger));
  mode mode_1 (
    .m(MODE), .Disaster_condition(flood_1_flood), .Decoded_disaster(decoder_1_flood), .nm(not_1_out),
    .OUTPUT(mode_1_output));
  mode mode_2 (
    .m(MODE), .Disaster_condition(cyclone_1_cyclone), .Decoded_disaster(decoder_1_cyclone), .nm(not_1_out),
    .OUTPUT(mode_2_output));
  mode mode_3 (
    .m(MODE), .Disaster_condition(earthquake_1_earthquake), .Decoded_disaster(decoder_1_earthquake),
    .nm(not_1_out), .OUTPUT(mode_3_output));
  mode mode_4 (
    .m(MODE), .Disaster_condition(tsunami_1_tsunami), .Decoded_disaster(decoder_1_tsunami), .nm(not_1_out),
    .OUTPUT(mode_4_output));
  LED FLOOD_2 (.in(mode_1_output));
  LED CYCLONE_2 (.in(mode_2_output));
  LED EARTHQUAKE_2 (.in(mode_3_output));
  LED TSUNAMI_2 (.in(mode_4_output));

  // Notes on the sheet:
  //   Rain
  //   MODE 
  //   0
  //   1
  //   Seismic
  //   INDEX
  //   TYPE
  //   UNIQUE DISASTER
  //   MULTI DISASTER
  //   Wind
  //   Sea Level
  //   INPUT
  //   00
  //   01
  //   10
  //   11
  //   Flood Condition
  //   Cyclone Condition
  //   Earthquake Condition
  //   Tsunami Condition
  //   IMPACT
  //   Low/None
  //   Medium
  //   High
  //   Very High
  //   DISASTER WARNING DEVICE (S1-T19)
  //   Priority Arrangement
  //   Decoded Disaster
  //   Mode Response
endmodule

module flood (
  input  [1:0] R1R0,
  input  [1:0] S1S0,
  input  [1:0] W1W0,
  input  [1:0] L1L0,
  output FLOOD
);

  wire and_1_out, comparator_1_eq, comparator_1_lt, comparator_2_eq, comparator_3_eq, comparator_3_gt,
       comparator_4_eq, comparator_4_gt, or_1_out, or_2_out, or_3_out, or_4_out;

  Comparator #(.width(2)) comparator_1 (.a(R1R0), .b(2'b10), .eq(comparator_1_eq), .lt(comparator_1_lt));  // open: gt
  Comparator #(.width(2)) comparator_2 (.a(R1R0), .b(2'b11), .eq(comparator_2_eq));  // open: gt, lt
  Comparator #(.width(2)) comparator_3 (.a(W1W0), .b(2'b10), .gt(comparator_3_gt), .eq(comparator_3_eq));  // open: lt
  Comparator #(.width(2)) comparator_4 (.a(L1L0), .b(2'b10), .gt(comparator_4_gt), .eq(comparator_4_eq));  // open: lt
  or or_1 (or_1_out, comparator_1_lt, comparator_1_eq);
  or or_2 (or_2_out, comparator_3_gt, comparator_3_eq);
  or or_3 (or_3_out, comparator_4_gt, comparator_4_eq);
  or or_4 (or_4_out, or_2_out, or_3_out);
  or or_5 (FLOOD, comparator_2_eq, and_1_out);
  and and_1 (and_1_out, or_1_out, or_4_out);

  // Notes on the sheet:
  //   Flood Condition
endmodule

module cyclone (
  input  [1:0] R1R0,
  input  [1:0] S1S0,
  input  [1:0] W1W0,
  input  [1:0] L1L0,
  output CYCLONE
);

  wire and_1_out, comparator_1_eq, comparator_1_gt, comparator_2_eq, comparator_2_lt, comparator_3_eq,
       comparator_4_eq, comparator_4_gt, or_1_out, or_2_out, or_3_out, or_4_out;

  Comparator #(.width(2)) comparator_1 (.a(R1R0), .b(2'b10), .gt(comparator_1_gt), .eq(comparator_1_eq));  // open: lt
  Comparator #(.width(2)) comparator_2 (.a(W1W0), .b(2'b10), .eq(comparator_2_eq), .lt(comparator_2_lt));  // open: gt
  Comparator #(.width(2)) comparator_3 (.a(W1W0), .b(2'b11), .eq(comparator_3_eq));  // open: gt, lt
  Comparator #(.width(2)) comparator_4 (.a(L1L0), .b(2'b10), .gt(comparator_4_gt), .eq(comparator_4_eq));  // open: lt
  or or_1 (or_1_out, comparator_1_gt, comparator_1_eq);
  or or_2 (or_2_out, comparator_2_lt, comparator_2_eq);
  or or_3 (or_3_out, comparator_4_gt, comparator_4_eq);
  or or_4 (or_4_out, or_1_out, or_3_out);
  and and_1 (and_1_out, or_4_out, or_2_out);
  or or_5 (CYCLONE, and_1_out, comparator_3_eq);

  // Notes on the sheet:
  //   Cyclone Condition
endmodule

module earthquake (
  input  [1:0] R1R0,
  input  [1:0] S1S0,
  input  [1:0] W1W0,
  input  [1:0] L1L0,
  output EARTHQUAKE
);

  or or_1 (EARTHQUAKE, S1S0[0], S1S0[1]);

  // Notes on the sheet:
  //   Earthquake Condition
endmodule

module tsunami (
  input  [1:0] R1R0,
  input  [1:0] S1S0,
  input  [1:0] W1W0,
  input  [1:0] L1L0,
  output TSUNAMI
);

  wire and_1_out;

  and and_1 (and_1_out, S1S0[0], S1S0[1]);
  or or_1 (TSUNAMI, and_1_out, L1L0[1]);

  // Notes on the sheet:
  //   Tsunami Condition
endmodule

module mode (
  input  m,
  input  Disaster_condition,
  input  Decoded_disaster,
  input  nm,
  output OUTPUT
);

  wire and_1_out, and_2_out;

  and and_1 (and_1_out, m, Disaster_condition);
  and and_2 (and_2_out, Decoded_disaster, nm);
  or or_1 (OUTPUT, and_1_out, and_2_out);

  // Notes on the sheet:
  //   Mode Response
endmodule

module priority_encoder (
  input  F,
  input  C,
  input  E,
  input  T,
  output SAFE___DANGER,
  output [1:0] Y1_Y0
);

  wire and_1_out, not_1_out, or_1_out;

  not not_1 (not_1_out, E);
  or or_1 (or_1_out, F, C);
  or or_2 (Y1_Y0[1], E, T);
  and and_1 (and_1_out, C, not_1_out);
  or or_3 (Y1_Y0[0], and_1_out, T);
  or or_4 (SAFE___DANGER, or_1_out, Y1_Y0[1]);

  // Notes on the sheet:
  //   Priority Encoder
endmodule

module decoder (
  input  Safe___Danger,
  input  [1:0] Y1_Y0,
  output FLOOD,
  output CYCLONE,
  output EARTHQUAKE,
  output TSUNAMI
);

  wire not_1_out, not_2_out;

  not not_1 (not_1_out, Y1_Y0[1]);
  not not_2 (not_2_out, Y1_Y0[0]);
  and and_1 (FLOOD, not_1_out, Safe___Danger, not_2_out);
  and and_2 (CYCLONE, not_1_out, Safe___Danger, Y1_Y0[0]);
  and and_3 (EARTHQUAKE, Y1_Y0[1], Safe___Danger, not_2_out);
  and and_4 (TSUNAMI, Y1_Y0[1], Safe___Danger, Y1_Y0[0]);

  // Notes on the sheet:
  //   Decoder
endmodule
